# Fritzing sketch Connections (saved by Fritzing 0.9.4)

parts:
  Part1 = PowerBoost 1000 Basic
  Part2 = Adafruit Adalogger FeatherWing [part_number="Adafruit #2922"]  # not connected
  Part3 = Adafruit FeatherWing Doubler [part_number="Adafruit #2890"]
  Boron1 = Particle Boron  # not connected
  Part4 = Lithium Ion Battery Pack 3.7V 6600mAh [part_number=353]
  SONAR1 = Maxbotix MaxSonar Ultrasonic Sensor (Hi-Res)
  DHT1 = DHT22 Humidity and Temperature Sensor
  Part5 = LIDAR-Lite

nets:
  +5V: Part1.VBAT, Part3.3V, Part4.negative, SONAR1.+5V, DHT1.VDD
  GND: Part1.GND, Part3.GND, SONAR1.GND, DHT1.GND, Part5.GND
  N1: Part1.ENABLE, Part3.J
  N2: Part1.5.0V, Part5.5V
  N3: Part3.I, SONAR1.PW
  N4: Part3.RX, Part5.SDA
  N5: Part3.MISO, Part5.SCL
  N6: Part3.C, DHT1.DATA
  N7: Part3.N$194, Part4.positive

custom parts:
  PowerBoost 1000 Basic: The PowerBoost 1000 is a little DC/DC boost converter module that can run from 1.8V batteries or higher, and convert the battery output to 5.2V DC for running your 5V projects. At its heart is a TPS61030 boost converter from TI. This boost converter chip has some really nice extras such as low battery detection, 4A internal switch, synchronous conversion, excellent efficiency, and 700KHz high-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
  Adafruit Adalogger FeatherWing: This is the Adalogger FeatherWing: it adds both a battery-backed Real Time Clock and micro SD card storage to any Feather main board. This FeatherWing will make it real easy to add datalogging to any of our existing Feathers. You get both an I2C real time clock (PCF8523) with 32KHz crystal and battery backup, and a microSD socket that connects to the SPI port pins (+ extra pin for CS). Tested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
  Adafruit FeatherWing Doubler: This is the FeatherWing Doubler - a prototyping add-on and more for all Feather boards. This is similar to our FeatherWing Proto except there are two! The magic of the Doubler comes when stacking a Feather and another board on top of the Doubler so you can work with both boards simultaneously side-by-side! The Doubler, like the Proto, has a duplicate breakout for each pin on a Feather, as well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
  Particle Boron: The Boron LTE is a powerful LTE CAT-M1 enabled development kit that can act as either a standalone cellular device or LTE enabled gateway, repeater, or endpoint for a Particle Mesh networks. Equipped with the Nordic nRF52840 and u-blox SARA 410 processors, the Boron has built-in battery charging circuitry which makes it easier to connect a Li-Po battery and 20 mixed signal GPIOs to interface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
  Lithium Ion Battery Pack 3.7V 6600mAh: This lithium ion pack is made of 3 balanced 2200mAh cells for a total of 6600mA capacity! The cells are connected in parallel and spot-welded to a protection circuit that provides over-voltage, under-voltage and over-current protection. Each cell can provide 0.5C of current (1.1 A per) so all together the peak current you can draw is over 3.3 Amps. Note that these batteries are not designed to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
  Maxbotix MaxSonar Ultrasonic Sensor (Hi-Res): Maxbotix MaxSonar Hi-Resolution Ultrasonic Sensor HRLV-EZ0, HRLV-EZ1, HRLV-EZ2, HRLV-EZ3, HRLV-EZ4
  LIDAR-Lite: PulsedLight LIDAR-Lite Sensor
